# Fritzing sketch schematic (saved by Fritzing 0.9.3b)

parts:
  Raspberry_Pi_1 = Raspberry Pi 3 [part_number=RPI-3-V1.2]
  S1 = Pushbutton [package="[THT]"]
  S2 = Pushbutton [package="[THT]"]
  S3 = Pushbutton [package="[THT]"]
  S4 = Pushbutton [package="[THT]"]
  S5 = Pushbutton [package="[THT]"]
  R1 = Resistor [tolerance=±5% resistance=330 package=THT]
  R2 = Resistor [tolerance=±5% resistance=2.2k package=THT]
  R3 = Resistor [tolerance=±5% resistance=6.8k package=THT]
  R4 = Resistor [tolerance=±5% resistance=15k package=THT]
  R5 = Resistor [tolerance=±5% resistance=39k package=THT]
  R6 = Resistor [tolerance=±5% resistance=220 package=THT]
  Part1 = Adafruit ADS1015 12Bit I2C ADC [part_number="Adafruit #1083"]

nets:
  3V3: Raspberry_Pi_1.3v3, Raspberry_Pi_1.3V3, R1.Pin_0, R2.Pin_0, R3.Pin_0, R4.Pin_0, R5.Pin_0, Part1.VDD
  N1: Raspberry_Pi_1.GPIO2, Part1.SDA
  N2: Raspberry_Pi_1.GPIO3, Part1.SCL
  N3: Raspberry_Pi_1.GIPO5, S1.Pin_2
  N4: Raspberry_Pi_1.GIPO6, S2.Pin_2
  N5: Raspberry_Pi_1.GIPO13, S4.Pin_2
  N6: Raspberry_Pi_1.GIPO19, S3.Pin_2
  N7: Raspberry_Pi_1.GIPO26, S5.Pin_2
  GND: Raspberry_Pi_1.GND, Raspberry_Pi_1.GIPO14, S1.Pin_3, S1.Pin_4, S2.Pin_3, S2.Pin_4, S3.Pin_3, S3.Pin_4, S4.Pin_3, S4.Pin_4, S5.Pin_3, S5.Pin_4, R6.Pin_1, Part1.GND
  N8: R1.Pin_1, R2.Pin_1, R3.Pin_1, R4.Pin_1, R5.Pin_1, R6.Pin_0, Part1.AIN0

custom parts:
  Adafruit ADS1015 12Bit I2C ADC: For microcontrollers without an analog-to-digital converter or when you want a higher-precision ADC, the ADS1015 provides 12-bit precision at 3300 samples/second over I2C. The chip can be configured as 4 single-ended input channels, or two differential channels. As a nice bonus, it even includes a programmable gain amplifier, up to x16, to help boost up smaller single/differential signals to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
